# Fritzing sketch stc89c51rc (saved by Fritzing 0.9.3b)
breadboards: 1

parts:
  C2 = Ceramic Capacitor [capacitance=22µF package="100 mil [THT, multilayer]"]
  XTAL1 = Crystal [frequency="16 Mhz" package=THT]
  USB_to_Serial/TTL_Adapter = USB TTL Serial Cable
  C1 = Ceramic Capacitor [capacitance=22µF package="100 mil [THT, multilayer]"]
  Resistor = Resistor [tolerance=±5% resistance=10k package=THT]
  Reset = Pushbutton [package="[THT]"]
  IC1 = IC, DIP package, 40 pins [chip_label=STC89C51RC]
  LED = LED - 5mm [color="White (4500K)" package="5 mm [THT]"]

nets:
  N1: C2.0, USB_to_Serial/TTL_Adapter.GND, C1.1, IC1.pin20, LED.cathode
  N2: C2.1, XTAL1.pin_0, IC1.pin18
  N3: XTAL1.pin_1, C1.0, IC1.pin19
  N4: USB_to_Serial/TTL_Adapter.RX, IC1.pin11
  N5: USB_to_Serial/TTL_Adapter.TX, IC1.pin10
  N6: USB_to_Serial/TTL_Adapter.5V, Reset.Pin_1, Reset.Pin_2, IC1.pin40
  N7: Resistor.Pin_0, LED.anode
  N8: Resistor.Pin_1, IC1.pin3
  N9: Reset.Pin_3, Reset.Pin_4, IC1.pin9
